# Fritzing sketch Sketch Self Balancing Robot (saved by Fritzing 0.8.7b)
breadboards: 1

parts:
  Part1 = Arduino Uno (Rev3)
  M1 = DC Motor
  M2 = DC Motor
  S1 = H-Bridge with L298N
  VCC1 = Battery
  Part2 = InvenSense MPU6050

nets:
  N1: Part1.A4/SDA, Part2.SDA
  N2: Part1.A5/SCL, Part2.SCL
  N3: Part1.D2, Part2.INT
  N4: Part1.D6_PWM, S1.IN1
  3V3: Part1.3V3, Part2.VCC
  GND: Part1.GND, S1.GND, VCC1.-, Part2.GND
  VIN: Part1.VIN, S1.12V, VCC1.+
  N5: M1.pin_1, M2.pin_1, S1.M1-02
  N6: M1.pin_2, M2.pin_2, S1.M1-01

custom parts:
  H-Bridge with L298N: h-bridge
